# Fritzing sketch Kitchen Dashboard Wiring Diagram (saved by Fritzing 0.9.5d)

parts:
  A1 = ESP32-S3-WROOM-1-N16R8 dev board
  Part1 = INMP441
  U1 = WS2812 RGB LED strip
  S1 = Toggle Switch [package=THT]

nets:
  N1: A1.Pin_1, A1.Pin_2, Part1.VDD
  N2: A1.Pin_4, A1.Pin_5, Part1.SD
  N3: A1.Pin_15, U1.DIN
  N4: A1.Pin_18, S1.L2
  N5: A1.Pin_21, U1.VCC
  N6: A1.Pin_22, A1.Pin_23, A1.Pin_44, Part1.L/R, U1.GND, S1.COM
  N7: A1.Pin_39, A1.Pin_40, Part1.SCK

notes:
  Custom Parts:
  https://forum.fritzing.org/t/im-looking-for-esp32-s3-n16r8/21946/2
  https://github.com/gcoulby/FritzingParts/blob/master/INMP441.fzpz
  https://forum.fritzing.org/t/ws2812-rgb-led-strip-matrix/6339
  Remember to solder the 5V Pad!
  https://smarthomecircle.com/How-I-created-my-voice-assistant-with-on-device-wake-word-using-home-assistant

custom parts:
  ESP32-S3-WROOM-1-N16R8 dev board: ESP32-S3 WIFI+BLE5.0 Development Board ESP32-S3-WROOM-1-N16R8(16M Flash/8SRAM).
  INMP441: This is a simple breakout board for the INMP441 I2S MEMS microphone.
  WS2812 RGB LED strip: WS2812 strip
